# Fritzing sketch ESPDeskClockandWeather (saved by Fritzing 0.9.3b)
breadboards: 1

parts:
  U1 = NodeMCU V1.0
  U2 = LCD-16X2 [package=lcd-16x2_nosilk]
  R1 = TRIMPOT [package=trimpot-5mm]

nets:
  N1: U1.D0, U2.RS
  N2: U1.D1, U2.E
  N3: U1.D2, U2.DB4
  N4: U1.D3, U2.DB5
  N5: U1.D4, U2.DB6
  GND: U1.GND, U2.VSS, U2.R_W, U2.K, R1.CCW
  N6: U1.D5, U2.DB7
  VIN: U1.Vin, U2.VDD, U2.A, R1.WIPER
  N7: U2.VO, R1.CW

custom parts:
  NodeMCU V1.0: ESP8266 based NodeMCU
